// Logisim project Domaci 2.circ as structural Verilog: 2 circuits, main circuit Domaci 2
module Domaci_2 (
  input  x1,
  input  x2,
  input  x3,
  input  x4,
  input  x5,
  output y
);

  wire nor_1_out, nor_2_out, nor_3_out, nor_4_out, nor_5_out, nor_6_out, nor_7_out, nor_8_out;

  nor nor_1 (nor_1_out, x3, x3);
  nor nor_2 (nor_2_out, x4, x4);
  nor nor_3 (nor_3_out, x2, x1);
  nor nor_4 (nor_4_out, nor_1_out, nor_2_out);
  nor nor_5 (nor_5_out, nor_3_out, nor_3_out);
  nor nor_6 (nor_6_out, nor_4_out, nor_4_out);
  nor nor_7 (nor_7_out, nor_6_out, x5);
  nor nor_8 (nor_8_out, nor_7_out, nor_7_out);
  nor nor_9 (y, nor_8_out, nor_5_out);

  // Notes on the sheet:
  //   Datum rodjenja: 21.03 = 2+1+0+3 = 6
endmodule

module Pocetno (
  input  x1,
  input  x2,
  input  x3,
  input  x4,
  input  x5,
  output y
);

  wire and_1_out, and_2_out, and_3_out, not_1_out, not_2_out, not_3_out;

  and and_1 (and_1_out, x3, x4);
  not not_1 (not_1_out, x5);
  not not_2 (not_2_out, x2);
  not not_3 (not_3_out, x1);
  and and_2 (and_2_out, and_1_out, not_1_out);
  and and_3 (and_3_out, not_2_out, not_3_out);
  and and_4 (y, and_2_out, and_3_out);
endmodule
