// Logisim project Vezbe 1.circ as structural Verilog: 10 circuits, main circuit Vezbe_1
module Vezbe_1 (
  input  X1,
  input  X2,
  output out_3
);

  wire not_1_out, not_2_out, or_1_out, or_2_out;

  // Probe on not_1_out
  not not_1 (not_1_out, X2);
  not not_2 (not_2_out, X1);
  // Probe on not_2_out
  or or_1 (or_1_out, X1, not_1_out);
  or or_2 (or_2_out, not_2_out, X2);
  // Probe on or_1_out
  // Probe on or_2_out
  and and_1 (out_3, or_1_out, or_2_out);
endmodule

module Vezbe_1_2 (
  input  X1,
  input  X2,
  output x
);

  wire not_1_out, not_2_out, or_1_out, or_2_out;

  not not_1 (not_1_out, X2);
  not not_2 (not_2_out, X1);
  or or_1 (or_1_out, X1, not_1_out);
  or or_2 (or_2_out, not_2_out, X2);
  and and_1 (x, or_1_out, or_2_out);
endmodule

module Vezbe_1_2_2 (
  input  X1,
  input  X2,
  output x
);

  wire nand_1_out, nand_2_out, nand_3_out, nand_4_out, nand_5_out;

  nand nand_1 (nand_1_out, X1, X1);
  nand nand_2 (nand_2_out, X2, X2);
  nand nand_3 (nand_3_out, nand_1_out, X2);
  nand nand_4 (nand_4_out, X1, nand_2_out);
  nand nand_5 (nand_5_out, nand_3_out, nand_4_out);
  nand nand_6 (x, nand_5_out, nand_5_out);
endmodule

module Vezbe_1_2_2_2 (
  input  X1,
  input  X2,
  input  X3,
  input  X4,
  output out_5
);

  wire vezbe_1_1_x, vezbe_1_2_x;

  Vezbe_1_2_2 vezbe_1_1 (.X1(X1), .X2(X2), .x(vezbe_1_1_x));
  Vezbe_1_2_2 vezbe_1_2 (.X1(X4), .X2(X3), .x(vezbe_1_2_x));
  Vezbe_1_2_2 vezbe_1_3 (.X1(vezbe_1_1_x), .X2(vezbe_1_2_x), .x(out_5));
endmodule

module Vezbe_1_2_2_2_2 (
  input  X1,
  input  X2,
  input  X3,
  input  X4,
  output x
);

  wire and_1_out, and_2_out, and_3_out, and_4_out, and_5_out, and_6_out, and_7_out, and_8_out, and_9_out,
       and_10_out, and_11_out, and_12_out, and_13_out, and_14_out, and_15_out, and_16_out, and_17_out,
       and_18_out, and_19_out, and_20_out, and_21_out, and_22_out, and_23_out, and_24_out, not_1_out,
       not_2_out, not_3_out, not_4_out, not_5_out, not_6_out, not_7_out, not_8_out, not_9_out, not_10_out,
       not_11_out, not_12_out, not_13_out, not_14_out, not_15_out, not_16_out, or_1_out, or_2_out, or_3_out,
       or_4_out, or_5_out, or_6_out;

  not not_1 (not_1_out, X1);
  and and_1 (and_1_out, not_1_out, not_2_out);
  not not_2 (not_2_out, X2);
  not not_3 (not_3_out, X3);
  and and_2 (and_2_out, not_3_out, not_4_out);
  not not_4 (not_4_out, X4);
  not not_5 (not_5_out, X1);
  and and_3 (and_3_out, not_5_out, not_6_out);
  not not_6 (not_6_out, X2);
  and and_4 (and_4_out, X3, X4);
  not not_7 (not_7_out, X1);
  and and_5 (and_5_out, not_7_out, X2);
  not not_8 (not_8_out, X3);
  and and_6 (and_6_out, not_8_out, X4);
  not not_9 (not_9_out, X1);
  and and_7 (and_7_out, not_9_out, X2);
  and and_8 (and_8_out, X3, not_10_out);
  not not_10 (not_10_out, X4);
  and and_9 (and_9_out, X1, not_11_out);
  not not_11 (not_11_out, X2);
  not not_12 (not_12_out, X3);
  and and_10 (and_10_out, not_12_out, X4);
  and and_11 (and_11_out, X1, not_13_out);
  not not_13 (not_13_out, X2);
  and and_12 (and_12_out, X3, not_14_out);
  not not_14 (not_14_out, X4);
  and and_13 (and_13_out, X1, X2);
  not not_15 (not_15_out, X3);
  and and_14 (and_14_out, not_15_out, not_16_out);
  not not_16 (not_16_out, X4);
  and and_15 (and_15_out, X1, X2);
  and and_16 (and_16_out, X3, X4);
  and and_17 (and_17_out, and_1_out, and_2_out);
  and and_18 (and_18_out, and_3_out, and_4_out);
  and and_19 (and_19_out, and_5_out, and_6_out);
  and and_20 (and_20_out, and_7_out, and_8_out);
  and and_21 (and_21_out, and_9_out, and_10_out);
  and and_22 (and_22_out, and_11_out, and_12_out);
  and and_23 (and_23_out, and_13_out, and_14_out);
  and and_24 (and_24_out, and_15_out, and_16_out);
  or or_1 (or_1_out, and_17_out, and_18_out);
  or or_2 (or_2_out, and_19_out, and_20_out);
  or or_3 (or_3_out, and_21_out, and_22_out);
  or or_4 (or_4_out, and_23_out, and_24_out);
  or or_5 (or_5_out, or_1_out, or_2_out);
  or or_6 (or_6_out, or_3_out, or_4_out);
  or or_7 (x, or_5_out, or_6_out);
endmodule

module Vezbe_1_2_2_2_2_2 (
  input  X1,
  input  X2,
  input  X3,
  input  X4,
  output x
);

  wire nand_1_out, nand_2_out, nand_3_out, nand_4_out, nand_5_out, nand_6_out, nand_7_out, nand_8_out,
       nand_9_out, nand_10_out, nand_11_out, nand_12_out, nand_13_out, nand_14_out, nand_15_out, nand_16_out,
       nand_17_out, nand_18_out, nand_19_out, nand_20_out, nand_21_out, nand_22_out, nand_23_out, nand_24_out;

  nand nand_1 (nand_1_out, X1, X1);
  nand nand_2 (nand_2_out, X2, X2);
  nand nand_3 (nand_3_out, X3, X3);
  nand nand_4 (nand_4_out, X4, X4);
  nand nand_5 (nand_5_out, X1, X1);
  nand nand_6 (nand_6_out, X2, X2);
  nand nand_7 (nand_7_out, X1, X1);
  nand nand_8 (nand_8_out, X3, X3);
  nand nand_9 (nand_9_out, X1, X1);
  nand nand_10 (nand_10_out, X4, X4);
  nand nand_11 (nand_11_out, X2, X2);
  nand nand_12 (nand_12_out, X3, X3);
  nand nand_13 (nand_13_out, X2, X2);
  nand nand_14 (nand_14_out, X4, X4);
  nand nand_15 (nand_15_out, X3, X3);
  nand nand_16 (nand_16_out, X4, X4);
  nand nand_17 (nand_17_out, nand_1_out, nand_2_out, nand_3_out, nand_4_out);
  nand nand_18 (nand_18_out, nand_5_out, nand_6_out, X3, X4);
  nand nand_19 (nand_19_out, nand_7_out, X2, nand_8_out, X4);
  nand nand_20 (nand_20_out, nand_9_out, X2, X3, nand_10_out);
  nand nand_21 (nand_21_out, X1, nand_11_out, nand_12_out, X4);
  nand nand_22 (nand_22_out, X1, nand_13_out, X3, nand_14_out);
  nand nand_23 (nand_23_out, X1, X2, nand_15_out, nand_16_out);
  nand nand_24 (nand_24_out, X1, X2, X3, X4);
  nand nand_25 (x, nand_17_out, nand_18_out, nand_19_out, nand_20_out, nand_21_out, nand_22_out, nand_23_out, nand_24_out);
endmodule

module Vezbe_1_2_comb (
  input  X1,
  input  X2,
  input  X3,
  input  X4,
  input  X5,
  input  X6,
  output x
);

  wire nand_1_out, nand_2_out, nand_3_out, nand_4_out, nand_5_out, nand_6_out, nand_7_out, nand_8_out,
       nand_9_out, nand_10_out, nand_11_out, nand_12_out, nand_13_out, nand_14_out, nand_15_out, nand_16_out,
       nand_17_out, nand_18_out, nand_19_out, nand_20_out, nand_21_out, nand_22_out, nand_23_out, nand_24_out;

  nand nand_1 (nand_1_out, X1, X1);
  nand nand_2 (nand_2_out, X2, X2);
  nand nand_3 (nand_3_out, X5, X5);
  nand nand_4 (nand_4_out, X4, X4);
  nand nand_5 (nand_5_out, X1, X1);
  nand nand_6 (nand_6_out, X2, X2);
  nand nand_7 (nand_7_out, X1, X1);
  nand nand_8 (nand_8_out, X3, X3);
  nand nand_9 (nand_9_out, X1, X1);
  nand nand_10 (nand_10_out, X4, X4);
  nand nand_11 (nand_11_out, X2, X2);
  nand nand_12 (nand_12_out, X3, X3);
  nand nand_13 (nand_13_out, X2, X2);
  nand nand_14 (nand_14_out, X4, X4);
  nand nand_15 (nand_15_out, X3, X3);
  nand nand_16 (nand_16_out, X6, X6);
  nand nand_17 (nand_17_out, nand_1_out, nand_2_out, nand_3_out, nand_4_out);
  nand nand_18 (nand_18_out, nand_5_out, nand_6_out, X3, X4);
  nand nand_19 (nand_19_out, nand_7_out, X2, nand_8_out, X4);
  nand nand_20 (nand_20_out, nand_9_out, X2, X3, nand_10_out);
  nand nand_21 (nand_21_out, X1, nand_11_out, nand_12_out, X6);
  nand nand_22 (nand_22_out, X1, nand_13_out, X3, nand_14_out);
  nand nand_23 (nand_23_out, X1, X2, nand_15_out, nand_16_out);
  nand nand_24 (nand_24_out, X1, X2, X3, X4);
  nand nand_25 (x, nand_17_out, nand_18_out, nand_19_out, nand_20_out, nand_21_out, nand_22_out, nand_23_out, nand_24_out);
endmodule

module Vezbe_1_3_Dekoder (
  input  X1,
  input  X2,
  input  X3,
  input  in_4,
  input  in_5,
  output D0,
  output D1,
  output D2,
  output D3,
  output D4,
  output D5,
  output D6,
  output D7
);

  wire vezbe_1_1_out_3;

  Decoder #(.select(3)) decoder_1 (
    .out0(D0), .out1(D1), .out2(D2), .out3(D3), .out4(D4), .out5(D5), .out6(D6), .out7(D7),
    .sel({X1, X2, X3}), .en(vezbe_1_1_out_3));
  Vezbe_1 vezbe_1_1 (.X1(in_5), .X2(in_4), .out_3(vezbe_1_1_out_3));
endmodule

module Vezbe_1_3_Dekoder_2 (
  input  X1,
  input  X2,
  input  X3,
  input  a,
  input  b,
  output D0,
  output D1,
  output D2,
  output D3,
  output D4,
  output D5,
  output D6,
  output D7
);

  wire and_1_out, and_2_out, and_3_out, and_4_out, and_5_out, and_6_out, and_7_out, and_8_out, not_1_out,
       not_2_out, not_3_out, not_4_out, not_5_out, not_6_out, not_7_out, not_8_out, not_9_out, not_10_out,
       not_11_out, not_12_out;

  not not_1 (not_1_out, X1);
  not not_2 (not_2_out, X2);
  not not_3 (not_3_out, X1);
  not not_4 (not_4_out, X2);
  not not_5 (not_5_out, X1);
  not not_6 (not_6_out, X1);
  not not_7 (not_7_out, X2);
  not not_8 (not_8_out, X2);
  and and_1 (and_1_out, X1, X2);
  not not_9 (not_9_out, X3);
  and and_2 (and_2_out, X1, X2);
  and and_3 (and_3_out, not_1_out, not_2_out);
  not not_10 (not_10_out, X3);
  and and_4 (and_4_out, not_3_out, not_4_out);
  and and_5 (and_5_out, not_5_out, X2);
  not not_11 (not_11_out, X3);
  and and_6 (and_6_out, not_6_out, X2);
  and and_7 (and_7_out, X1, not_7_out);
  not not_12 (not_12_out, X3);
  and and_8 (and_8_out, X1, not_8_out);
  and and_9 (D6, and_1_out, not_9_out);
  and and_10 (D7, and_2_out, X3);
  and and_11 (D0, and_3_out, not_10_out);
  and and_12 (D1, and_4_out, X3);
  and and_13 (D2, and_5_out, not_11_out);
  and and_14 (D3, and_6_out, X3);
  and and_15 (D4, and_7_out, not_12_out);
  and and_16 (D5, and_8_out, X3);
endmodule

module Vezbe_1_3_Dekoder_2_2 (
  input  X1,
  input  X2,
  input  X3,
  input  a,
  input  b,
  output D0,
  output D1,
  output D2,
  output D3,
  output D4,
  output D5,
  output D6,
  output D7
);

  wire nand_1_out, nand_2_out, nand_3_out, nand_4_out, nand_5_out, nand_6_out, nand_7_out, nand_8_out,
       nand_9_out, nand_10_out, nand_11_out, nand_12_out, nand_13_out, nand_14_out, nand_15_out, nand_16_out,
       nand_17_out, nand_18_out, nand_19_out, nand_20_out;

  nand nand_1 (nand_1_out, X1, X1);
  nand nand_2 (nand_2_out, X2, X2);
  nand nand_3 (nand_3_out, X3, X3);
  nand nand_4 (nand_4_out, X1, X1);
  nand nand_5 (nand_5_out, X2, X2);
  nand nand_6 (nand_6_out, X1, X1);
  nand nand_7 (nand_7_out, X3, X3);
  nand nand_8 (nand_8_out, X1, X1);
  nand nand_9 (nand_9_out, X2, X2);
  nand nand_10 (nand_10_out, X3, X3);
  nand nand_11 (nand_11_out, X2, X2);
  nand nand_12 (nand_12_out, X3, X3);
  nand nand_13 (nand_13_out, X1, X2, X3);
  nand nand_14 (nand_14_out, nand_1_out, nand_2_out, nand_3_out);
  nand nand_15 (nand_15_out, nand_4_out, nand_5_out, X3);
  nand nand_16 (nand_16_out, nand_6_out, X2, nand_7_out);
  nand nand_17 (nand_17_out, nand_8_out, X2, X3);
  nand nand_18 (nand_18_out, X1, nand_9_out, nand_10_out);
  nand nand_19 (nand_19_out, X1, nand_11_out, X3);
  nand nand_20 (nand_20_out, X1, X2, nand_12_out);
  nand nand_21 (D7, nand_13_out, nand_13_out);
  nand nand_22 (D0, nand_14_out, nand_14_out);
  nand nand_23 (D1, nand_15_out, nand_15_out);
  nand nand_24 (D2, nand_16_out, nand_16_out);
  nand nand_25 (D3, nand_17_out, nand_17_out);
  nand nand_26 (D4, nand_18_out, nand_18_out);
  nand nand_27 (D5, nand_19_out, nand_19_out);
  nand nand_28 (D6, nand_20_out, nand_20_out);
endmodule
